# Fritzing sketch Arturito Circuit Diagram_Zulfikar Sepyan (saved by Fritzing 0.9.10b)
breadboards: 1

parts:
  Part1 = Arduino Uno (Rev3)
  J1 = Piezo Speaker
  HC-SR04_Sensor_1 = HC-SR04 Ultrasonic Distance Sensor
  R1 = PHOTOCELL [package=photocell]
  LED2 = LED - 5mm [color="Red (633nm)" current=0.030 package="5 mm [THT]"]
  LED3 = LED - 5mm [color="Green (555nm)" current=0.030 package="5 mm [THT]"]
  LED4 = LED - 5mm [color="Yellow (585nm)" current=0.030 package="5 mm [THT]"]
  Part2 = Soil Moisture Sensor
  U1 = POT [knob_status=50% power=0.5W package=pot_alpha_rv16af-20]
  LED5 = smd LED [color="Blue (430nm)" package="0603 [SMD]"]
  R2 = Resistor [tolerance=±5% resistance=10k package="0603 [SMD]"]
  R3 = Resistor [tolerance=±5% power=0.25 resistance=220 package=THT]
  R4 = Resistor [tolerance=±5% power=0.25 resistance=220 package=THT]
  Sensore_PIR_HC-SR502 = HC-SR501 Body Sensor Module
  R6 = Resistor [tolerance=±5% resistance=220 package="0603 [SMD]"]
  R7 = Resistor [tolerance=±5% power=0.25 resistance=220 package=THT]
  R8 = Resistor [tolerance=±5% resistance=220 package="0603 [SMD]"]
  LCD1 = LCD screen

nets:
  N1: Part1.A0, Part2.SIG
  N2: Part1.A1, R1.P$1, R2.Pin_0
  N3: Part1.A2, R7.Pin_1
  N4: Part1.A3, R4.Pin_1
  N5: Part1.A4/SDA, R3.Pin_1
  N6: Part1.D8, LCD1.DB6
  N7: Part1.D9_PWM, LCD1.DB7
  N8: Part1.D11_PWM/MOSI, LCD1.E
  N9: Part1.D12/MISO, LCD1.RS
  N10: Part1.D13/SCK, R6.Pin_0
  GND: Part1.GND, J1.pin1, HC-SR04_Sensor_1.GND, LED2.cathode, LED3.cathode, LED4.cathode, Part2.GND, U1.A, LED5.cathode, R2.Pin_1, Sensore_PIR_HC-SR502.GND, LCD1.VSS, LCD1.R/W, LCD1.LED-
  N11: Part1.D2, J1.pin2
  N12: Part1.D3_PWM, Sensore_PIR_HC-SR502.OUT
  N13: Part1.D4, HC-SR04_Sensor_1.TRIG
  N14: Part1.D5_PWM, HC-SR04_Sensor_1.ECHO
  N15: Part1.D6_PWM, LCD1.DB4
  N16: Part1.D7, LCD1.DB5
  3V3: Part1.3V3, Part2.VCC
  VCC: Part1.5V, HC-SR04_Sensor_1.VCC, R1.P$2, U1.E, Sensore_PIR_HC-SR502.VCC, R8.Pin_1, LCD1.VDD
  N17: LED2.anode, R3.Pin_0
  N18: LED3.anode, R7.Pin_0
  N19: LED4.anode, R4.Pin_0
  N20: U1.S, LCD1.V0
  N21: LED5.anode, R6.Pin_1
  N22: R8.Pin_0, LCD1.LED+

custom parts:
  HC-SR501 Body Sensor Module: Pyroelectric Infrared PIR Motion Sensor Detector Module

// code stored in the sketch: final coding challenge 1.ino
// Resistive Soil Moisture Sensor + LCD Output + buzzer + PIR Sensor + LEDs + URM Sensor + Photoresistor for plant communication device
// author: Zulfikar Sepyan
// link to TinkerCAD circuit board:
// https://www.tinkercad.com/things/4Bric4f2zdT-copy-of-arturitozulfikar-sepyan/editel?sharecode=C7pGVBI0aVoO3drpbGcjRWeWqLMva66GQIUtVi4JYGk


#include <LiquidCrystal.h>                              // make LCD output available
LiquidCrystal LCD(12, 11, 6, 7, 8, 9);                  // digital pin on the Arduino for LCD


// greeting messages program memory
const byte greetingMessages = 15;
char* names[greetingMessages] = {
  "Hello, you!",
  "Bipbipbip bepbop",
  "No doubt",
  "You look good",
  "Enough water, Pa",
  "Enough water, Ma",
  "All too well",
  "Coffee at 9?",
  "Hahahaha funny",
  "Yes",
  "Ask again later",
  "Good day init?",
  "Better call Saul",
  "Ask GPT!",
  "I am good"
};


// pins
const int moisturePin = A0;                           
const int buzzerPin = 2;                             
const int PIRPin = 3;                                 
const int blueLedPin = 13;                             
const int greenLedPin = A2;
const int yellowLedPin = A3;
const int redLedPin = A4;
const int URMTrigPin = 4;
const int URMEchoPin = 5;
const int photoresistorPin = A1;


// additional variables for PIR Sensor
int percentageCurr = 100;                               // initial value
const int calibrationTime = 30;


// additional variables for photoresistor
int sensorValue;                                        // to hold sensor value
int sensorLow = 1023;                                   // to calibrate low value
int sensorHigh = 0;                                     // to calibrate high value


// additional variables for soil moisture sensor
int moistureValue;                                      // to hold sensor value
int moistureLow = 0;                                    // minimum level of soil moisture
int moistureHigh = 740;                                 // maximum level of soil moisture as what the sensor read


// additional variables for URM sensor
long duration;
int distance;
int distanceLow = 400;                                  // maximum range of URM sensor is 400cm
int distanceHigh = 2;                                   // minimum range of URM sensor is 2cm


void setup() {
  
  Serial.begin(9600);                                   // start communication with Serial Monitor 
  LCD.begin(16, 2);                                     // start communication with LCD 16 by 2 characters


  // digital pins setup
  pinMode(PIRPin, INPUT);                               // set PIR sensor as the input
  pinMode(buzzerPin, OUTPUT);                           // set buzzer as the output
  pinMode(blueLedPin, OUTPUT);                          // set the led as the output
  pinMode(greenLedPin, OUTPUT);                         // set the led as the output
  pinMode(yellowLedPin, OUTPUT);                        // set the led as the output
  pinMode(redLedPin, OUTPUT);                           // set the led as the output
  pinMode(URMTrigPin, OUTPUT);                          // set the URM sensor's trig as the output
  pinMode(URMEchoPin, INPUT);                           // set the URM sensor's echo as the input


  randomSeed(analogRead(0));                            // to generate random number
  
  // sensors calibration (for 30 seconds)
  digitalWrite(PIRPin, LOW);                            // initial condition of PIR sensor
  LCD.setCursor(0, 0);                                  // show calibration status on LCD
  LCD.print("Clbrtng Sensors");                        
  while (millis() < 30000) {                            // millis 30000 = 30s. do this loop for sensor calibration in 30s duration.
    for (int i = 0; i < calibrationTime; i++) {
      
      sensorValue = analogRead(photoresistorPin);
      if (sensorValue > sensorHigh) {                  
        
        sensorHigh = sensorValue;                       // the highest reading during calibration become maximum number of photoresistor
      }
      if (sensorValue < sensorLow) {
        
        sensorLow = sensorValue;                        // the lowest reading during calibration become minimum number of photoresistor
      }


      int process = map(i, 0, 30, 0, 100);              // display percentage of calibration process on the LCD
      LCD.setCursor(0, 1);
      LCD.print(process);
      LCD.print("%");
      delay(1000);
    }
  }
  LCD.clear();
  LCD.print("Calibration Done");                        // show that calibration has done on the LCD
  delay(1000);
  LCD.clear();
  delay(50); 
}


// tone randomizer mode 1: low freq --> high freq == happy tone. random function will choose one number between the range.
void phrase1() {


  int k = random(1000,2000);
  digitalWrite(blueLedPin, HIGH);
  for (int i = 0; i <= random(100,2000); i++){


    tone(buzzerPin, k + (-i * 2));
    delay(random(.9,2));
  }
  digitalWrite(blueLedPin, LOW);
  for (int i = 0; i <= random(100,1000); i++){


    tone(buzzerPin, k + (i * 10));
    delay(random(.92));
  }
}


// tone randomizer mode 2: high freq --> low freq == sad tone
void phrase2() {


    int k = random(1000,2000);
    digitalWrite(blueLedPin, HIGH);  
    for (int i = 0; i <= random(100,2000); i++){
        
        tone(buzzerPin, k + (i * 2));          
        delay(random(.9,2));             
    } 
    digitalWrite(blueLedPin, LOW);   
    for (int i = 0; i <= random(100,1000); i++){
        
        tone(buzzerPin, k + (-i * 10));          
        delay(random(.9,2));             
    } 
}


void measure_it() {                                     // function for URM sensor to read distance
  digitalWrite(URMTrigPin, LOW);
  delayMicroseconds(2);


  digitalWrite(URMTrigPin, HIGH);
  delayMicroseconds(10);
  digitalWrite(URMTrigPin, LOW);


  duration = pulseIn(URMEchoPin, HIGH);
  distance = duration * 0.034/2;                        // divided by speed of sound in microsecond
}


void loop() {
  
  // map the highest value and the lowest value of sensor readings into the specified ranges
  moistureValue = analogRead(moisturePin);
  int percentage = map(moistureValue, moistureLow, moistureHigh, 0, 100);
  sensorValue = analogRead(photoresistorPin);
  int pitchDivider = map(sensorValue, sensorLow, sensorHigh, 10, 1); // it will become "divider", and bright result will divide smaller than dim result. thus it is mapped this way.


  digitalWrite(yellowLedPin, LOW);                      // initial state of yellow led is off for all moisture condition, unless it is dim or cloudy 
  if (pitchDivider > 5) {                               // if it is dim or cloudy, yellow led turned on


    digitalWrite(yellowLedPin, HIGH);
  }
  LCD.setCursor(0, 1);                                  // show moisture sensor reading in percentage on the LCD
  LCD.print("Percent: ");
  LCD.print(percentage);
  LCD.print("%");                                       


  if (percentage <= 40) {                                // if soil moisture level lower than 20%


    digitalWrite(greenLedPin, LOW);
    digitalWrite(redLedPin, HIGH);                      // red led turned on as the indicator when soil moisture level is low
    LCD.setCursor(0, 0);
    LCD.print("Water me, please");                      // the "water me" message when soil moisture level is low
    
    if (digitalRead(PIRPin) == HIGH) {                  // (additionally) if someone around when the soil moisture level is low. else, it won't do nothing more.
      measure_it();                                     // measure the distance with the person approaching
      // map the measured distance to 1 - 10 range to be used as delay multiplier for sound variation. addtnly, distance > 100 will be regarded as 10.
      int distancePercent = map(distance, 2, 100, 1, 10);


      // produce the sound --> sound of R2D2
      // 2 parts of R2D2 sound
      // 1st part: tone randomizer function called (phrase 1 and phrase 2). switch function will choose 1 of 7 variations provided.
      switch (random(1,7)) {
        
        case 1:phrase1(); break;
        case 2:phrase2(); break;
        case 3:phrase1(); delay(distancePercent); phrase2(); break;
        case 4:phrase1(); delay(distancePercent); phrase2(); delay(distancePercent); phrase1(); break;
        case 5:phrase1(); delay(distancePercent); phrase2(); delay(distancePercent); phrase1(); delay(distancePercent); phrase2(); delay(distancePercent); phrase1(); break;
        case 6:phrase2(); delay(distancePercent); phrase1(); delay(distancePercent); phrase2(); break;
      }


      // 2nd part: 
      for (int i = 0; i <= random(3, 9); i++){
      
        digitalWrite(blueLedPin, HIGH);  
        tone(buzzerPin, random(300, 4000) / pitchDivider);         
        delay(random(70, 100) * pitchDivider / 5);  
        digitalWrite(blueLedPin, LOW);           
        noTone(buzzerPin);         
        delay(random(1, 30) * distancePercent);             
      } 
      noTone(buzzerPin);         
      delay(random(100, 200) * distancePercent); 
    }
  }


  else if (percentage - percentageCurr > 30) {          // if there is a sudden rise in soil moisture level --> assumably, someone water it


    digitalWrite(greenLedPin, HIGH);                    // green led turn on when soil moisture level is good
    digitalWrite(redLedPin, LOW);
    LCD.setCursor(0, 0);
    LCD.print("Thank you");                             // show "thank you" message on the LCD when the plant is watered
    LCD.setCursor(0, 1);
    LCD.print("so much, mate!");


    for (int i = 0; i < 1; i++){                        // play the sound (do re mi fa sol la si do) when the plant is watered


      tone(buzzerPin, 251.626); delay(200); noTone(buzzerPin); delay(100);
      tone(buzzerPin, 294.33); delay(200); noTone(buzzerPin); delay(100);
      tone(buzzerPin, 327.03); delay(200); noTone(buzzerPin); delay(100);
      tone(buzzerPin, 348.83); delay(200); noTone(buzzerPin); delay(100);
      tone(buzzerPin, 392.44); delay(200); noTone(buzzerPin); delay(100);
      tone(buzzerPin, 436.04); delay(200); noTone(buzzerPin); delay(100);
      tone(buzzerPin, 490.55); delay(200); noTone(buzzerPin); delay(100);
      tone(buzzerPin, 523.25); delay(200); noTone(buzzerPin); delay(100);        
    }
    delay(2000);
  }


  else {                                                // (percentage >= 40) if soil moisture is in the good level


    digitalWrite(redLedPin, LOW);
    digitalWrite(greenLedPin, HIGH);                    // green led turned on when soil moisture level is good
    LCD.setCursor(0, 0);                              
    LCD.print("Soil Moisture");                         // show this character on the first line of the LCD 
    
    if (digitalRead(PIRPin) == HIGH) {                  // (additionally) when someone is around when the soil moisture level is good. else, do nothing more.


      if (pitchDivider <= 5) {                          // when it is BRIGHT, someone is around, and soil moisture is good
        
        LCD.setCursor(0,0);
        LCD.print(names[random(0,greetingMessages)]);   // show "greeting message" on the LCD that chose randomly from the program memory
        phrase1();                                      // happy tone played = phrase 1
        delay (200);
      }


      else {                                            // (pitchDivider > 5) but when the surrounding is DIM instead
        
        digitalWrite(greenLedPin, LOW);                 // set the green led off so that the yellow led as light indicator can catch the attention
        LCD.setCursor(0,0);
        LCD.print("A bit dark init?");                  // show "worry message" on the LCD
        phrase2();                                      // sad tone played = phrase 2
        delay (200);
      }


      noTone (buzzerPin);
      delay(2000);
    }
  }
  percentageCurr = percentage;                          // store percentage value in another variable
  delay(1000);
  LCD.clear();                                          // clear the LCD from any output
}
