# Fritzing sketch DnDHat (saved by Fritzing 0.9.10b)
circuit board: 8.46667cm x 5.64444cm
breadboards: 2

parts:
  Arduino_UNO = Arduino Uno (Rev3)
  NEMA_17 = Stepper Motor - Bipolar
  L298N1 = L298N DC motor driver
  IR = TSOP312.., 314.. [package=THT]
  buzzerPin = Piezo Speaker
  led1Pin = LED - 5mm [color="Red (633nm)" current=0.030 package="5 mm [THT]"]
  ledPin = smd LED [color="Blue (430nm)" package="1206 [SMD]"]
  R = Resistor [tolerance=±5% resistance=220 package="2512 [SMD]"]
  R1 = Resistor [tolerance=±5% resistance=220 package="2512 [SMD]"]
  URM = HC-SR04 Ultrasonic Distance Sensor
  PIR_1 = PIR sensor
  PIR_2 = PIR sensor
  PIR_3 = PIR sensor
  PIR_4 = PIR sensor
  Power_plug1 = Power plug

nets (from the breadboard view):
  N1: Arduino_UNO.A0, buzzerPin.pin2
  N2: Arduino_UNO.A1, R.Pin_0
  N3: Arduino_UNO.D8, PIR_1.SIG
  N4: Arduino_UNO.D9_PWM, PIR_2.SIG
  N5: Arduino_UNO.D10_PWM/SS, PIR_3.SIG
  N6: Arduino_UNO.D11_PWM/MOSI, PIR_4.SIG
  N7: Arduino_UNO.D12/MISO, R1.Pin_0
  N8: Arduino_UNO.D13/SCK, IR.Data
  GND: Arduino_UNO.GND, L298N1.GND, IR.GND, buzzerPin.pin1, led1Pin.cathode, ledPin.cathode, URM.GND, PIR_1.GND, PIR_2.GND, PIR_3.GND, PIR_4.GND, Power_plug1.GND
  N9: Arduino_UNO.D2, URM.ECHO
  N10: Arduino_UNO.D3_PWM, URM.TRIG
  N11: Arduino_UNO.D4, L298N1.IN1
  N12: Arduino_UNO.D5_PWM, L298N1.IN2
  N13: Arduino_UNO.D6_PWM, L298N1.IN3
  N14: Arduino_UNO.D7, L298N1.IN4
  VDD: Arduino_UNO.5V, IR.Vs, URM.VCC, PIR_1.VDD, PIR_2.VDD, PIR_3.VDD, PIR_4.VDD
  N15: NEMA_17.A, L298N1.OUT1
  N16: NEMA_17.C, L298N1.OUT2
  N17: NEMA_17.B, L298N1.OUT3
  N18: NEMA_17.D, L298N1.OUT4
  12V: L298N1.12V, Power_plug1.VCC
  N19: led1Pin.anode, R1.Pin_1
  N20: ledPin.anode, R.Pin_1

notes:
  12V power input
  5V power input

custom parts:
  L298N DC motor driver: 2x DC motor driver with 78M05 positive voltage regulator (7..35 V) L298N: max 46 V, 2 A Set 5 V Enable jumper to enable 5 V regultor (needed for the L298N) and +5 V output at screw terminal or supply external +5 V at screw terminal Set ENA and/or ENB to +5 V to enable motor permanently or supply ENA and/or ENB with PWM signal IN1 and IN2 set rotation directory for motor A (OUT1/OUT2) IN2 and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
