# Fritzing sketch UnhopefulReality (saved by Fritzing 0.9.10b)
breadboards: 3

parts:
  Part1 = Arduino Uno (Rev3)
  HC-SR04_Sensor_1 = HC-SR04 Ultrasonic Distance Sensor
  4_Channel_Relay1 = 4 Channel Power Relay
  WATER_PUMP1 = water pump/motor
  WATER_PUMP2 = water pump/motor
  LCD1 = LCD screen
  LED1 = RGB LED (com. cathode, rbg) [package="5 mm [THT]"]
  LED2 = RGB LED (com. cathode, rbg) [package="5 mm [THT]"]
  J1 = Piezo Speaker
  J2 = Piezo Speaker
  Part2 = Arduino Uno (Rev3)
  IR1 = TSOP312.., 314.. [package=THT]
  D1 = LTE-302 [package=lte-302]
  D2 = LTE-302 [package=lte-302]
  IR2 = TSOP312.., 314.. [package=THT]
  LED3 = smd LED [color="Blue (430nm)" package="0603 [SMD]"]
  S4 = Momentary Switch [package=ksa_sealed_tac_switch]
  S5 = Momentary Switch [package=ksa_sealed_tac_switch]
  Grove1 = Grove 3 Axis Digital Accelerometer 16g
  R1 = Resistor [tolerance=±5% resistance=220 package="1206 [SMD]"]
  6v = Battery
  6v_2 = Battery
  R2 = Resistor [tolerance=±5% resistance=220 package="1206 [SMD]"]
  R3 = Resistor [tolerance=±5% resistance=220 package="1206 [SMD]"]
  LED4 = smd LED [color="Green (555nm)" package="0603 [SMD]"]
  LED5 = smd LED [color="Red (633nm)" package="0603 [SMD]"]
  LED6 = smd LED [color="Blue (430nm)" package="0603 [SMD]"]
  S6 = Momentary Switch [package=ksa_sealed_tac_switch]
  R4 = Resistor [tolerance=±5% resistance=220 package="1206 [SMD]"]
  R5 = Resistor [tolerance=±5% resistance=220 package="1206 [SMD]"]
  R6 = Resistor [tolerance=±5% resistance=220 package="1206 [SMD]"]
  R7 = Resistor [tolerance=±5% resistance=220 package="1206 [SMD]"]
  R8 = Rotary Potentiometer (Large) [maximum_resistance=100kΩ knob_status=50% power=0.5W package=THT]
  R9 = Resistor [tolerance=±5% resistance=220 package="1206 [SMD]"]

nets:
  N1: Part1.A0, IR1.Data
  N2: Part1.A1, D1.A
  N3: Part1.A2, LED3.anode
  N4: Part1.A3, J1.pin2
  N5: Part1.D8, S5.3
  N6: Part1.D9_PWM, LED2.green_anode
  N7: Part1.D10_PWM/SS, LED2.red_anode
  N8: Part1.D12/MISO, 4_Channel_Relay1.IN2
  N9: Part1.D13/SCK, 4_Channel_Relay1.IN4
  N10: Part1.A4/SDA, Grove1.SDA
  N11: Part1.A5/SCL, Grove1.SCL
  N12: Part1.D2, HC-SR04_Sensor_1.ECHO
  N13: Part1.D3_PWM, HC-SR04_Sensor_1.TRIG
  N14: Part1.D5_PWM, LED1.green_anode
  N15: Part1.D6_PWM, LED1.red_anode
  N16: Part1.D7, S4.3
  VCC: Part1.5V, HC-SR04_Sensor_1.VCC, IR1.Vs, S4.2, S5.2, Grove1.VCC
  GND: Part1.GND, HC-SR04_Sensor_1.GND, 4_Channel_Relay1.GND, WATER_PUMP1.pin_1, WATER_PUMP2.pin_1, LED1.common_cathode, LED2.common_cathode, J1.pin1, IR1.GND, D1.C, Grove1.GND, R1.Pin_0, 6v.-, R2.Pin_0, R3.Pin_0
  N17: 4_Channel_Relay1.VCC, 4_Channel_Relay1.COM, 6v_2.+
  N18: 4_Channel_Relay1.NO#21, WATER_PUMP2.pin_2
  N19: 4_Channel_Relay1.NO#27, WATER_PUMP1.pin_2
  VSS: LCD1.VSS, LCD1.R/W, LCD1.LED-, J2.pin1, D2.A, IR2.GND, R4.Pin_1, R5.Pin_1, R6.Pin_1, R7.Pin_1, R8.leg1
  N20: LCD1.VDD, IR2.Vs, S6.3, R8.leg2, R9.Pin_1
  N21: LCD1.V0, R8.wiper
  N22: LCD1.RS, Part2.D11_PWM/MOSI
  N23: LCD1.E, Part2.D10_PWM/SS
  N24: LCD1.DB4, Part2.D6_PWM
  N25: LCD1.DB5, Part2.D7
  N26: LCD1.DB6, Part2.D8
  N27: LCD1.DB7, Part2.D9_PWM
  N28: LCD1.LED+, R9.Pin_0
  N29: J2.pin2, Part2.A3
  N30: Part2.A0, IR2.Data
  N31: Part2.A1, D2.C
  N32: Part2.A2, LED6.anode
  N33: Part2.D3_PWM, S6.2
  N34: Part2.D4, LED4.anode
  N35: Part2.D5_PWM, LED5.anode
  N36: LED3.cathode, R1.Pin_1
  N37: S4.4, R3.Pin_1
  N38: S5.4, R2.Pin_1
  N39: 6v.+, 6v_2.-
  N40: LED4.cathode, R5.Pin_0
  N41: LED5.cathode, R6.Pin_0
  N42: LED6.cathode, R7.Pin_0
  N43: S6.1, R4.Pin_0

custom parts:
  4 Channel Power Relay: A 4 channel power relay. The module operates at 5V.
  water pump/motor: WATER PUMP BY ARDUBLOCKTR
